// Logisim project Meio Somador.circ as structural Verilog: 1 circuit, main circuit Meio Somador
module Meio_Somador (
  input  A,
  input  B,
  output Carry,
  output Soma
);

  and and_1 (Carry, A, A, B);
  xor xor_1 (Soma, A, B);
endmodule
