// Logisim project Somador Completo.circ as structural Verilog: 1 circuit, main circuit main
module main (
  input  carry_anterior,
  input  A,
  input  B,
  output Carry,
  output Soma
);

  wire and_1_out, and_2_out, xor_1_out;

  and and_1 (and_1_out, A, B);
  xor xor_1 (xor_1_out, A, B);
  xor xor_2 (Soma, carry_anterior, xor_1_out);
  and and_2 (and_2_out, carry_anterior, carry_anterior, xor_1_out);
  or or_1 (Carry, and_1_out, and_2_out);
endmodule
