// Logisim project contador-digital.circ as structural Verilog: 1 circuit, main circuit main
module main (
  output [3:0] out_1,
  output [3:0] out_2,
  output [3:0] out_3,
  output [3:0] out_4,
  output [3:0] out_5,
  output [3:0] out_6,
  output out_7,
  output carry,
  output carry_2,
  output carry_3
);

  wire and_1_out, clock_1_out, counter_3_carry, counter_5_carry;

  Counter #(.width(4), .max('h2), .trigger("falling")) counter_1 (
    .Q(out_1), .carry(out_7), .clk(carry), .clr(and_1_out));  // open: load, D, count
  Hex_Digit_Display hex_digit_display_1 (.value(out_1));  // open: dp
  Hex_Digit_Display hex_digit_display_2 (.value(out_2));  // open: dp
  Counter #(.width(4), .max('h9), .trigger("falling")) counter_2 (
    .Q(out_2), .carry(carry), .clk(counter_3_carry), .clr(and_1_out));  // open: load, D, count
  and and_1 (and_1_out, out_1[1], out_2[2]);
  Hex_Digit_Display hex_digit_display_3 (.value(out_3));  // open: dp
  Counter #(.width(4), .max('h5), .trigger("falling")) counter_3 (
    .Q(out_3), .carry(counter_3_carry), .clk(carry_2));  // open: load, D, count, clr
  Hex_Digit_Display hex_digit_display_4 (.value(out_4));  // open: dp
  Counter #(.width(4), .max('h9), .trigger("falling")) counter_4 (
    .Q(out_4), .carry(carry_2), .clk(counter_5_carry));  // open: load, D, count, clr
  Counter #(.width(4), .max('h5), .trigger("falling")) counter_5 (
    .Q(out_5), .carry(counter_5_carry), .clk(carry_3));  // open: load, D, count, clr
  Hex_Digit_Display hex_digit_display_5 (.value(out_5));  // open: dp
  Counter #(.width(4), .max('h9), .trigger("falling")) counter_6 (
    .Q(out_6), .carry(carry_3), .clk(clock_1_out));  // open: load, D, count, clr
  Clock clock_1 (.out(clock_1_out));
  Hex_Digit_Display hex_digit_display_6 (.value(out_6));  // open: dp
endmodule
