// Logisim project exercicio-2.circ as structural Verilog: 1 circuit, main circuit main
module main (
  input  A2,
  input  A1,
  input  A0,
  output D0,
  output D1,
  output D2,
  output D3
);

  buf and_1 (D0, ~A0);  // AND_Gate AND_Gate
  buf and_2 (D1, A0);  // AND_Gate AND_Gate
  and and_3 (D2, ~A0, A1);  // AND_Gate
  and and_4 (D3, A0, A1);
endmodule
