// Logisim project exercicio-3.circ as structural Verilog: 1 circuit, main circuit main
module main (
  input  [1:0] in_1,
  output D0,
  output D1,
  output D2,
  output D3
);

  Decoder #(.select(2)) decoder_1 (.out0(D0), .out1(D1), .out2(D2), .out3(D3), .sel(in_1));  // open: en
endmodule
