// Logisim project exercicio-4.circ as structural Verilog: 2 circuits, main circuit main
module main (
  input  [1:0] in_1,
  output D0,
  output D1,
  output D2,
  output D3
);

  Decoder #(.select(2)) decoder_1 (.out0(D0), .out1(D1), .out2(D2), .out3(D3), .sel(in_1));  // open: en
endmodule

module decodificador_3bits (
  input  [2:0] in_1,
  output D0,
  output out_3,
  output D2,
  output D3,
  output D4,
  output D5,
  output D6,
  output D7
);

  Decoder #(.select(3)) decoder_1 (
    .out0(D0), .out1(out_3), .out2(D2), .out3(D3), .out4(D4), .out5(D5), .out6(D6), .out7(D7), .sel(in_1));  // open: en
endmodule
