// Logisim project exercicio-2.circ as structural Verilog: 1 circuit, main circuit main
module main (
  input  A,
  input  B,
  input  C,
  output S
);

  wire and_1_out, and_2_out, nand_1_out, not_1_out;

  not not_1 (not_1_out, A);
  and and_1 (and_1_out, A, C);
  nand nand_1 (nand_1_out, B, C);
  and and_2 (and_2_out, not_1_out, B, C);
  or or_1 (S, and_1_out, nand_1_out, and_2_out);
endmodule
