// Logisim project exercicio-3.circ as structural Verilog: 1 circuit, main circuit main
module main (
  input  A,
  input  B,
  input  C,
  input  D,
  output S
);

  wire and_1_out, nand_1_out, not_1_out;

  and and_1 (and_1_out, A, B);
  not not_1 (not_1_out, C);
  // AND_Gate and_2 has open pins: in0=C, in1=D, out=open
  nand nand_1 (nand_1_out, C, D);
  or or_1 (S, and_1_out, not_1_out, nand_1_out);
endmodule
