// Logisim project exercicio-4.circ as structural Verilog: 1 circuit, main circuit main
module main (
  input  X,
  input  Y,
  input  W,
  output Z
);

  wire not_1_out, or_1_out;

  not not_1 (not_1_out, Y);
  or or_1 (or_1_out, not_1_out, W);
  and and_1 (Z, X, or_1_out);
endmodule
