// Logisim project exercicio-5.circ as structural Verilog: 1 circuit, main circuit main
module main (
  input  x1,
  input  x1_2,
  input  x1_3,
  input  x1_4,
  output x1_5,
  output x1_6
);

  wire and_1_out, and_2_out, and_3_out, and_4_out, not_1_out, not_2_out, not_3_out, not_4_out;

  not not_1 (not_1_out, x1);
  not not_2 (not_2_out, x1_2);
  not not_3 (not_3_out, x1_3);
  not not_4 (not_4_out, x1_4);
  buf and_1 (and_1_out, x1_2);  // AND_Gate
  buf and_2 (and_2_out, x1);  // AND_Gate
  buf and_3 (and_3_out, x1_4);  // AND_Gate
  buf and_4 (and_4_out, x1_3);  // AND_Gate
  or or_1 (x1_5, and_1_out, and_2_out);
  xor xor_1 (x1_6, and_3_out, and_4_out);
endmodule
