// Logisim project exercicio-7.circ as structural Verilog: 1 circuit, main circuit main
module main (
  input  [3:0] A0,
  input  [3:0] B0,
  output [3:0] Sub0,
  output B0_2
);

  wire [3:0] negator_1_out;

  Negator #(.width(4)) negator_1 (.in(B0), .out(negator_1_out));
  Adder #(.width(4)) adder_1 (.a(A0), .b(negator_1_out), .out(Sub0), .cout(B0_2));  // open: cin
endmodule
