// Logisim project exercicio-8.circ as structural Verilog: 1 circuit, main circuit main
module main (
  input  [3:0] A0,
  input  [3:0] B0,
  output [3:0] C0,
  output [3:0] S0
);

  Multiplier #(.width(4)) multiplier_1 (.a(A0), .b(B0), .out(S0), .cout(C0));  // open: cin
endmodule
