// Logisim project exercicio-9-(sem-sinal).circ as structural Verilog: 1 circuit, main circuit main
module main (
  input  [3:0] A0,
  input  [3:0] B0,
  output Greater,
  output Equal,
  output Less
);

  Comparator #(.width(4), .mode("unsigned")) comparator_1 (.a(A0), .b(B0), .gt(Greater), .eq(Equal), .lt(Less));
endmodule
